# Fritzing sketch BP (saved by Fritzing 0.8.7b)
breadboards: 1

parts:
  Onderdeel1 = Arduino Uno (Rev3)
  U1 = 74HC595 [package="DIP16 [THT]"]
  7_Segment1 = 7 Segment Display
  R1 = Resistor [tolerance=±5% resistance=220 package=THT]
  R2 = Resistor [tolerance=±5% resistance=220 package=THT]
  R3 = Resistor [tolerance=±5% resistance=220 package=THT]
  R4 = Resistor [tolerance=±5% resistance=220 package=THT]
  R5 = Resistor [tolerance=±5% resistance=220 package=THT]
  R6 = Resistor [tolerance=±5% resistance=220 package=THT]
  R7 = Resistor [tolerance=±5% resistance=220 package=THT]
  R8 = Resistor [tolerance=±5% resistance=220 package=THT]
  U2 = 74HC595 [package="DIP16 [THT]"]
  R9 = Resistor [tolerance=±5% resistance=220 package=THT]
  R10 = Resistor [tolerance=±5% resistance=220 package=THT]
  R11 = Resistor [tolerance=±5% resistance=220 package=THT]
  R12 = Resistor [tolerance=±5% resistance=220 package=THT]
  R13 = Resistor [tolerance=±5% resistance=220 package=THT]
  R14 = Resistor [tolerance=±5% resistance=220 package=THT]
  LED1 = LED - 5mm [color="Green (555nm)" package="5 mm [THT]"]
  LED2 = LED - 5mm [color="Orange (620nm)" package="5 mm [THT]"]
  LED3 = LED - 5mm [color="Red (633nm)" package="5 mm [THT]"]
  LED4 = LED - 5mm [color="Green (555nm)" package="5 mm [THT]"]
  LED5 = LED - 5mm [color="Red (633nm)" package="5 mm [THT]"]
  LED6 = LED - 5mm [color="Orange (620nm)" package="5 mm [THT]"]
  S1 = Pushbutton [package="[THT]"]
  S2 = Pushbutton [package="[THT]"]
  S3 = Pushbutton [package="[THT]"]
  R15 = Photocell (LDR) [package=THT]
  J1 = Basic Servo
  C1 = Electrolytic Capacitor [capacitance=1µF package="100 mil [THT, electrolytic]"]
  R16 = Resistor [tolerance=±5% resistance=10k package=THT]
  J2 = Piezo Speaker
  R17 = Resistor [tolerance=±5% resistance=220 package=THT]
  R19 = Resistor [tolerance=±5% resistance=10k package=THT]
  R20 = Resistor [tolerance=±5% resistance=10k package=THT]
  R21 = Resistor [tolerance=±5% resistance=10k package=THT]

nets:
  N1: Onderdeel1.A0, R15.pin_1, R16.Pin_0
  N2: Onderdeel1.D8, U2.SH_CP
  N3: Onderdeel1.D9_PWM, U2.ST_CP
  N4: Onderdeel1.D10_PWM/SS, U2.DS
  N5: Onderdeel1.D11_PWM/MOSI, S3.Pin_1, S3.Pin_2, R20.Pin_1
  N6: Onderdeel1.D12/MISO, S2.Pin_1, S2.Pin_2, R19.Pin_1
  N7: Onderdeel1.D13/SCK, S1.Pin_1, S1.Pin_2, R21.Pin_1
  N8: Onderdeel1.D3_PWM, J1.pulse
  N9: Onderdeel1.D4, R17.Pin_1
  N10: Onderdeel1.D5_PWM, U1.SH_CP
  N11: Onderdeel1.D6_PWM, U1.ST_CP
  N12: Onderdeel1.D7, U1.DS
  N13: U1.Q1, LED2.anode
  N14: U1.Q2, LED1.anode
  N15: U1.Q3, LED5.anode
  N16: U1.Q4, LED6.anode
  N17: U1.Q5, LED4.anode
  GND: U1.GND, U1.OE, 7_Segment1.common_anode, U2.GND, U2.OE, R9.Pin_1, R10.Pin_1, R11.Pin_1, R12.Pin_0, R13.Pin_0, R14.Pin_0, S1.Pin_3, S1.Pin_4, S2.Pin_3, S2.Pin_4, S3.Pin_3, S3.Pin_4, J1.gnd, C1.-, R16.Pin_1, J2.pin1
  VCC: U1.MR, U1.VCC, U2.MR, U2.VCC, R15.pin_0, J1.vcc, C1.+, R19.Pin_0, R20.Pin_0, R21.Pin_0
  N18: U1.Q0, LED3.anode
  N19: 7_Segment1.Segment_E, R5.Pin_1
  N20: 7_Segment1.Segment_D, R6.Pin_1
  N21: 7_Segment1.Segment_C, R4.Pin_0
  N22: 7_Segment1.Segment_DP, R3.Pin_0
  N23: 7_Segment1.Segment_B, R2.Pin_0
  N24: 7_Segment1.Segment_A, R1.Pin_0
  N25: 7_Segment1.Segment_F, R8.Pin_1
  N26: 7_Segment1.Segment_G, R7.Pin_1
  N27: R1.Pin_1, U2.Q0
  N28: R2.Pin_1, U2.Q1
  N29: R3.Pin_1, U2.Q7
  N30: R4.Pin_1, U2.Q2
  N31: R5.Pin_0, U2.Q4
  N32: R6.Pin_0, U2.Q3
  N33: R7.Pin_0, U2.Q6
  N34: R8.Pin_0, U2.Q5
  N35: R9.Pin_0, LED6.cathode
  N36: R10.Pin_0, LED4.cathode
  N37: R11.Pin_0, LED5.cathode
  N38: R12.Pin_1, LED2.cathode
  N39: R13.Pin_1, LED3.cathode
  N40: R14.Pin_1, LED1.cathode
  N41: J2.pin2, R17.Pin_0
